# Fritzing sketch blueboy (saved by Fritzing 0.9.6b)
breadboards: 1

parts:
  LLC1 = Logic Level Converter [package="Breakout board"]
  BT1 = Bluetooth HC-06u [package=THT]
  R2 = Resistor [tolerance=±5% resistance=10k package="0603 [SMD]"]
  R3 = Resistor [tolerance=±5% resistance=10k package="0603 [SMD]"]
  LSM303AGR1 = Adafruit LSM303AGR
  Part2 = Adafruit LSM6DS33 6-DoF Accel + Gyro IMU [part_number="Adafruit #4480"]
  TP1 = TP4056 [chip_label=TP4056 package="DIP (Dual Inline) [THT]"]
  BAT1 = 18650 battery holder [package=battery-18650-kit]
  J1 = Dagu DGServo 9g header (male) [package=THT]
  Part1 = Arduino Uno (Rev3)
  S1 = Toggle Switch [package=THT]
  R4 = Resistor [tolerance=±5% resistance=2k package="0603 [SMD]"]

nets:
  N1: LLC1.LV1, LSM303AGR1.SCL, Part2.SCL, J1.Vcc
  N2: LLC1.LV2, LSM303AGR1.SDA, Part2.SDA, J1.gnd
  VCC: LLC1.LV, LSM303AGR1.VCC, Part2.VCC, Part1.3V3
  GND: LLC1.L-GND, LLC1.H-GND, BT1.GND, LSM303AGR1.GND, Part2.GND, TP1.pin6, J1.pulse, Part1.GND
  N3: LLC1.LV4, BT1.TXD
  N4: LLC1.HV4, Part1.D8
  VCC_2: LLC1.HV, BT1.VCC, R2.Pin_0, R3.Pin_0, Part1.5V
  N5: LLC1.HV2, R2.Pin_1, Part1.A4/SDA
  N6: LLC1.HV1, R3.Pin_1, Part1.A5/SCL
  N7: BT1.RXD, Part1.D9_PWM
  N8: TP1.pin3, S1.COM
  N9: TP1.pin4, BAT1.+
  N10: TP1.pin5, BAT1.-
  N11: Part1.D4, R4.Pin_0
  N12: Part1.RESET, R4.Pin_1
  N13: Part1.VIN, S1.L2

notes:
  MSP430
  Left: SDA
  Mid: SCL
  Right: GND

custom parts:
  Logic Level Converter: 5V to/from 3.3V logic level converter
  Bluetooth HC-06u: Bluetooth HC-06 - face up, pins down 16.5mm x 37.5mm PCB
  Adafruit LSM303AGR: He told you "Go West, young maker!" - but you don't know which way is West! Ah, if only you had this triple-axis accelerometer/magnetometer compass module. Inside are two sensors, one is a classic 3-axis accelerometer, which can tell you which direction is down towards the Earth (by measuring gravity). The other is a magnetometer that can sense where the strongest magnetic force is coming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
  Adafruit LSM6DS33 6-DoF Accel + Gyro IMU: Add motion and orientation sensing to your Arduino project with this affordable 6 Degree of Freedom (6-DoF) sensor with sensors from ST. The board includes an LSM6DS33, a 6-DoF IMU accelerometer + gyro. The 3-axis accelerometer, can tell you which direction is down towards the Earth (by measuring gravity) or how fast the board is accelerating in 3D space. The 3-axis gyroscope that can measure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
  TP4056: A DIP stand-in part for whatever IC you want. With 6 pins on a 300mil dual inline package (DIP) footprint.
  18650 battery holder: 18650 Battery Holder
